# Fritzing sketch leonardo keypad 4x4 membrane (saved by Fritzing 0.9.3b)

parts:
  Part1 = Arduino Leonardo (Rev3b)
  Part2 = 4x4 Keypad [part_number=101207]

nets:
  N1: Part1.D0/RX, Part2.8
  N2: Part1.D1/TX, Part2.7
  N3: Part1.D2/SDA, Part2.6
  N4: Part1.D3_PWM/SCL, Part2.5
  N5: Part1.D4/A6, Part2.4
  N6: Part1.D5_PWM, Part2.3
  N7: Part1.D6_PWM/A7, Part2.2
  N8: Part1.D7, Part2.1

custom parts:
  4x4 Keypad: Matrix membrane keypad 4x4
